// Logisim project 1-bit full adder circuit.circ as structural Verilog: 1 circuit, main circuit main
module main (
  input  A,
  input  B,
  input  Cin,
  input  A_2,
  input  B_2,
  input  B_3,
  input  Cin_2,
  input  A_3,
  input  Cin_3
);

  wire and_1_out, and_2_out, and_3_out, or_1_out, or_2_out, xor_1_out, xor_2_out;

  xor xor_1 (xor_1_out, A, B);
  and and_1 (and_1_out, A_2, B_2);
  and and_2 (and_2_out, B_3, Cin_2);
  and and_3 (and_3_out, A_3, Cin_3);
  or or_1 (or_1_out, and_1_out, and_2_out);
  xor xor_2 (xor_2_out, xor_1_out, Cin);
  or or_2 (or_2_out, or_1_out, and_3_out);
  LED SUM (.in(xor_2_out));
  LED Cout (.in(or_2_out));
endmodule
